# Fritzing sketch Fritzing Circuit (saved by Fritzing 0.9.1b)
breadboards: 1

parts:
  Part1 = Arduino Uno (Rev3)
  S1 = Pushbutton [package="[THT]"]
  R2 = Resistor [tolerance=±5% resistance=220 package="0805 [SMD]"]
  R3 = Resistor [tolerance=±5% resistance=220 package="0805 [SMD]"]
  R4 = Resistor [tolerance=±5% resistance=220 package="0805 [SMD]"]
  LED1 = RGB LED (com. anode, rbg) [package="5 mm [THT]"]
  R5 = Resistor [tolerance=±5% resistance=10k package="0805 [SMD]"]

nets:
  N1: Part1.D9_PWM, R4.Pin_1
  N2: Part1.D10_PWM/SS, R3.Pin_1
  N3: Part1.D11_PWM/MOSI, R2.Pin_1
  N4: Part1.GND, S1.Pin_1, S1.Pin_2
  N5: Part1.D2, S1.Pin_3, S1.Pin_4, R5.Pin_0
  N6: Part1.5V, LED1.common_anode, R5.Pin_1
  N7: R2.Pin_0, LED1.red_cathode
  N8: R3.Pin_0, LED1.blue_cathode
  N9: R4.Pin_0, LED1.green_cathode
